# Fritzing sketch Power Board (saved by Fritzing 0.9.2b)

parts:
  IC1 = SO08 [chip_label=LT6105 package=SO]
  R2 = Resistor [tolerance=±5% resistance=100 package="0805 [SMD]"]
  R3 = Resistor [tolerance=±5% resistance=100 package="0805 [SMD]"]
  R1 = Resistor [tolerance=±5% resistance=1 package="0805 [SMD]"]

nets:
  N1: IC1.1, R2.Pin_0
  N2: IC1.8, R3.Pin_0
  N3: R2.Pin_1, R1.Pin_1
  N4: R3.Pin_1, R1.Pin_0
