# Fritzing sketch UROV 2016 Sam_wiring (saved by Fritzing 0.9.2b)
breadboards: 3

parts:
  Part1 = Arduino Mega 2560 (Rev3)
  Part2 = Arduino Mega 2560 (Rev3)
  U1 = MAX485 [package=dil08]
  MD09B1 = A4988 Stepper Motor Driver Carrier  # not connected
  Power_plug1 = Power plug
  J1 = Basic Servo
  J2 = Basic Servo
  J3 = Basic Servo
  J4 = Basic Servo
  IC1 = IC, DIP package, 24 pins [chip_label="NTE4097B Multiplexer"]  # not connected
  Part3 = 9 Degrees of Freedom - Sensor Stick
  IC3 = IC, DIP package, 8 pins [chip_label=Pressure]

nets (from the schematic view):
  N1: Part1.D21/SCL, Part2.D21/SCL, Part2.SCL, Part3.SCL
  N2: Part1.D20/SDA, Part1.SDA, Part2.D20/SDA, Part2.SDA, Part3.SDA
  1 to RX3: Part1.D15/RX3, U1.RO
  4 to TX3: Part1.D14/TX3, U1.DI
  AREF: Part1.AREF, J1.vcc, J2.vcc, J3.vcc, J4.vcc
  GND: Part1.GND, Part2.GND, U1.GND, Power_plug1.GND, IC3.pin2
  Servo1: Part1.D13_PWM, J1.pulse
  Servo2: Part1.D12_PWM, J2.pulse
  Servo3: Part1.D10_PWM
  Servo4: Part1.D9_PWM
  5V: Part1.IOREF, Part1.VIN, Part2.IOREF, U1.VCC, Part3.VCC
  2/3 to 2PWM: Part1.D2_PWM, U1.RE, U1.DE
  VIN: Part2.VIN, Power_plug1.VCC
  N3: Part2.D45, IC3.pin6
  N4: Part2.D50, IC3.pin8
  N5: Part2.D51, IC3.pin7
  N6: Part2.D52, IC3.pin1
  GND_2: J1.gnd, J2.gnd, J3.gnd, J4.gnd
  3.3V: IC3.pin5

notes:
  Power
  Accessories
  Topside
  Master
  Slave
  This is a representation of the motors; not the actual servos.
