# Fritzing sketch UROV 2016 wiring (saved by Fritzing 0.9.2b)
breadboards: 3

parts:
  Part1 = Arduino Mega 2560 (Rev3)
  Part2 = Arduino Mega 2560 (Rev3)
  Part3 = 9 Degrees of Freedom - Sensor Stick
  U1 = MAX485 [package=dil08]
  MD09B1 = A4988 Stepper Motor Driver Carrier  # not connected
  Power_plug1 = Power plug
  Pressure_sensor = IC, DIP package, 8 pins [chip_label=Pressure]  # not connected
  J1 = Basic Servo
  J2 = Basic Servo
  J3 = Basic Servo
  J4 = Basic Servo
  J5 = Basic Servo
  J6 = Basic Servo
  IC1 = IC, DIP package, 24 pins [chip_label="NTE4097B Multiplexer"]  # not connected

nets:
  N1: Part1.D21/SCL, Part1.SCL, Part2.D21/SCL, Part3.SCL
  N2: Part1.D20/SDA, Part1.SDA, Part2.D20/SDA, Part3.SDA
  N3: Part1.D15/RX3, U1.A
  N4: Part1.D14/TX3, U1.B
  VCC: Part1.AREF, J1.vcc, J2.vcc, J3.vcc, J4.vcc, J5.vcc, J6.vcc
  GND: Part1.GND, Part2.GND, Power_plug1.GND, J1.gnd, J2.gnd, J3.gnd, J4.gnd, J5.gnd, J6.gnd
  N5: Part1.D13_PWM, J1.pulse
  N6: Part1.D12_PWM, J2.pulse
  N7: Part1.D11_PWM, J3.pulse
  N8: Part1.D10_PWM, J4.pulse
  N9: Part1.D9_PWM, J6.pulse
  N10: Part1.D8_PWM, J5.pulse
  VIN: Part1.VIN, Part2.VIN, Power_plug1.VCC
  5V: Part2.5V, Part3.VCC

notes:
  Power
  Accessories
  Topside
